// Logisim project Milestone1.circ as structural Verilog
module OneBitAdder (
  input  A,
  input  B,
  input  C_in,
  output S,
  output C_out
);

  wire and_1_out, and_2_out, and_3_out, and_4_out, and_5_out, and_6_out, and_7_out, not_1_out, not_2_out,
       not_3_out;

  not not_1 (not_1_out, A);
  not not_2 (not_2_out, B);
  not not_3 (not_3_out, C_in);
  and and_1 (and_1_out, not_1_out, not_2_out, C_in);
  and and_2 (and_2_out, not_1_out, B, not_3_out);
  and and_3 (and_3_out, A, not_2_out, not_3_out);
  and and_4 (and_4_out, A, B, C_in);
  and and_5 (and_5_out, B, C_in);
  and and_6 (and_6_out, A, C_in);
  and and_7 (and_7_out, A, B);
  or or_1 (S, and_1_out, and_2_out, and_3_out, and_4_out);
  or or_2 (C_out, and_5_out, and_6_out, and_7_out);
endmodule

module ALU_Ctrl (
  input  I30,
  input  I14,
  input  I13,
  input  I12,
  input  I6,
  input  I5,
  input  I4,
  output ALU_Ctrl3,
  output ALU_Ctrl2,
  output ALU_Ctrl1,
  output ALU_Ctrl0,
  output ALU_Src
);

  wire and_2_out, not_1_out, not_2_out, not_3_out, not_4_out, not_5_out;

  not not_1 (not_1_out, I14);
  not not_2 (not_2_out, I13);
  not not_3 (not_3_out, I12);
  not not_4 (not_4_out, I5);
  not not_5 (not_5_out, I4);
  and and_1 (ALU_Ctrl2, I30, not_2_out, I5);
  or or_1 (ALU_Ctrl1, not_2_out, not_5_out);
  and and_2 (and_2_out, I13, not_3_out);
  or or_2 (ALU_Src, not_4_out, not_5_out);
  or or_3 (ALU_Ctrl0, not_1_out, and_2_out);

  assign ALU_Ctrl3 = 1'b0;
endmodule

module ALU (
  input  [3:0] ALU_Ctrl_in,
  input  A,
  input  B,
  input  C_in,
  output C_out,
  output R
);

  wire and_1_out, and_2_out, and_3_out, and_4_out, and_5_out, and_6_out, and_7_out, and_8_out, and_9_out,
       and_10_out, and_11_out, not_1_out, not_2_out, not_3_out, not_4_out, not_5_out;

  not not_1 (not_1_out, ALU_Ctrl_in[1]);
  not not_2 (not_2_out, ALU_Ctrl_in[0]);
  not not_3 (not_3_out, A);
  not not_4 (not_4_out, B);
  not not_5 (not_5_out, C_in);
  and and_1 (and_1_out, not_3_out, C_in);
  and and_2 (and_2_out, not_3_out, B);
  or or_1 (C_out, and_1_out, and_2_out, and_3_out);
  and and_3 (and_3_out, B, C_in);
  and and_4 (and_4_out, not_1_out, A, B, C_in);
  and and_5 (and_5_out, not_1_out, ALU_Ctrl_in[0], B);
  and and_6 (and_6_out, not_1_out, ALU_Ctrl_in[0], A);
  and and_7 (and_7_out, ALU_Ctrl_in[1], not_2_out, not_3_out, B);
  and and_8 (and_8_out, ALU_Ctrl_in[1], not_2_out, A, not_4_out);
  and and_9 (and_9_out, ALU_Ctrl_in[2], not_3_out, not_4_out, C_in);
  and and_10 (and_10_out, ALU_Ctrl_in[2], not_3_out, B, not_5_out);
  and and_11 (and_11_out, ALU_Ctrl_in[2], A, not_4_out, not_5_out);
  OneBitAdder onebitadder_1 (.A(A), .B(B), .C_in(C_in), .S(R), .C_out(C_out));
  or or_2 (R, and_4_out, and_5_out, and_6_out, and_7_out, and_8_out, and_9_out, and_10_out, and_11_out);
endmodule

module FourBALU (
  input  [3:0] A,
  input  [3:0] B,
  input  C_in,
  input  [3:0] ALU_Ctrl_in,
  output R0,
  output R1,
  output R2,
  output C_out,
  output R3
);

  wire alu_1_c_out, alu_2_c_out, alu_3_c_out;

  ALU alu_1 (.ALU_Ctrl_in(ALU_Ctrl_in), .A(A[0]), .B(B[0]), .C_in(C_in), .C_out(alu_1_c_out), .R(R0));
  ALU alu_2 (.ALU_Ctrl_in(ALU_Ctrl_in), .A(A[1]), .B(B[1]), .C_in(alu_1_c_out), .C_out(alu_2_c_out), .R(R1));
  ALU alu_3 (.ALU_Ctrl_in(ALU_Ctrl_in), .A(A[2]), .B(B[2]), .C_in(alu_2_c_out), .C_out(alu_3_c_out), .R(R2));
  ALU alu_4 (.ALU_Ctrl_in(ALU_Ctrl_in), .A(A[3]), .B(B[3]), .C_in(alu_3_c_out), .C_out(C_out), .R(R3));
endmodule

module ALU32B (
  input  [3:0] ALU_Ctrl_in,
  input  [3:0] A0,
  input  [3:0] B0,
  input  C_in,
  input  [3:0] A1,
  input  [3:0] B1,
  input  [3:0] A2,
  input  [3:0] B2,
  input  [3:0] A3,
  input  [3:0] B3,
  input  [3:0] A4,
  input  [3:0] B4,
  input  [3:0] A5,
  input  [3:0] B5,
  input  [3:0] A6,
  input  [3:0] B6,
  input  [3:0] A7,
  input  [3:0] B7,
  output R0,
  output R1,
  output R2,
  output R3,
  output R4,
  output R5,
  output R6,
  output R7,
  output R8,
  output R9,
  output R10,
  output R11,
  output R12,
  output R13,
  output R14,
  output R15,
  output R16,
  output R17,
  output R18,
  output R19,
  output R20,
  output R21,
  output R22,
  output R23,
  output R24,
  output R25,
  output R26,
  output R27,
  output R28,
  output R29,
  output R30,
  output R31,
  output C_out
);

  wire fourbalu_1_c_out, fourbalu_2_c_out, fourbalu_3_c_out, fourbalu_4_c_out, fourbalu_5_c_out,
       fourbalu_6_c_out, fourbalu_7_c_out;

  FourBALU fourbalu_1 (
    .A(A0), .B(B0), .C_in(C_in), .ALU_Ctrl_in(ALU_Ctrl_in), .R0(R0), .R1(R1), .R2(R2),
    .C_out(fourbalu_1_c_out), .R3(R3));
  FourBALU fourbalu_2 (
    .A(A1), .B(B1), .C_in(fourbalu_1_c_out), .ALU_Ctrl_in(ALU_Ctrl_in), .R0(R4), .R1(R5), .R2(R6),
    .C_out(fourbalu_2_c_out), .R3(R7));
  FourBALU fourbalu_3 (
    .A(A2), .B(B2), .C_in(fourbalu_2_c_out), .ALU_Ctrl_in(ALU_Ctrl_in), .R0(R8), .R1(R9), .R2(R10),
    .C_out(fourbalu_3_c_out), .R3(R11));
  FourBALU fourbalu_4 (
    .A(A3), .B(B3), .C_in(fourbalu_3_c_out), .ALU_Ctrl_in(ALU_Ctrl_in), .R0(R12), .R1(R13), .R2(R14),
    .C_out(fourbalu_4_c_out), .R3(R15));
  FourBALU fourbalu_5 (
    .A(A4), .B(B4), .C_in(fourbalu_4_c_out), .ALU_Ctrl_in(ALU_Ctrl_in), .R0(R16), .R1(R17), .R2(R18),
    .C_out(fourbalu_5_c_out), .R3(R19));
  FourBALU fourbalu_6 (
    .A(A5), .B(B5), .C_in(fourbalu_5_c_out), .ALU_Ctrl_in(ALU_Ctrl_in), .R0(R20), .R1(R21), .R2(R22),
    .C_out(fourbalu_6_c_out), .R3(R23));
  FourBALU fourbalu_7 (
    .A(A6), .B(B6), .C_in(fourbalu_6_c_out), .ALU_Ctrl_in(ALU_Ctrl_in), .R0(R24), .R1(R25), .R2(R26),
    .C_out(fourbalu_7_c_out), .R3(R27));
  FourBALU fourbalu_8 (
    .A(A7), .B(B7), .C_in(fourbalu_7_c_out), .ALU_Ctrl_in(ALU_Ctrl_in), .R0(R28), .R1(R29), .R2(R30),
    .C_out(C_out), .R3(R31));
endmodule
